# Fritzing sketch débimètre (saved by Fritzing 0.9.6b)
breadboards: 1

parts:
  WeMos_D1_Mini1 = WeMos D1 Mini
  S1 = Reed switch [package=THT]

nets:
  N1: WeMos_D1_Mini1.D1, WeMos_D1_Mini1.D2, S1.pin_2
  N2: WeMos_D1_Mini1.G, S1.pin_1

notes:
  Mesure de débit installation solaire thermique, 1.0.1
