# Fritzing sketch Mesure_courant_clip_v3 (saved by Fritzing 0.9.3b)
breadboards: 1

parts:
  WeMos_D1_Mini1 = WeMos D1 Mini
  U2 = Adafruit ADS1115 16Bit I2C ADC [part_number=ADS1115]
  C1 = Electrolytic Capacitor [capacitance=0.1mF package="100 mil [THT, electrolytic]"]
  R4 = Vertical Resistor [tolerance=±5% resistance=2.2k package=THT]
  C2 = Electrolytic Capacitor [capacitance=0.1mF package="100 mil [THT, electrolytic]"]
  C3 = Electrolytic Capacitor [capacitance=0.1mF package="100 mil [THT, electrolytic]"]
  C4 = Electrolytic Capacitor [capacitance=0.1mF package="100 mil [THT, electrolytic]"]
  J1 = Camdenboss CTB0158-8 [part_number=CTB0158-8 package=THT]
  R5 = Vertical Resistor [tolerance=±5% resistance=2.2k package=THT]
  R6 = Vertical Resistor [tolerance=±5% resistance=2.2k package=THT]
  R7 = Vertical Resistor [tolerance=±5% resistance=2.2k package=THT]
  D1 = Schottky Diode [part_number=1N5817 package="300 mil [THT]"]
  D2 = Schottky Diode [part_number=1N5817 package="300 mil [THT]"]
  D3 = Schottky Diode [part_number=1N5817 package="300 mil [THT]"]
  D4 = Schottky Diode [part_number=1N5817 package="300 mil [THT]"]

nets:
  3V3: WeMos_D1_Mini1.3V3, U2.VDD
  N1: WeMos_D1_Mini1.D1, U2.SCL
  N2: WeMos_D1_Mini1.D2, U2.SDA
  GND: WeMos_D1_Mini1.G, U2.GND, C1.-, R4.Pin_1, C2.-, C3.-, C4.-, J1.pin2, J1.pin4, J1.pin6, J1.pin8, R5.Pin_1, R6.Pin_1, R7.Pin_1
  N3: U2.AIN3, C1.+, R4.Pin_0, D1.cathode
  N4: U2.AIN2, C2.+, R5.Pin_0, D2.cathode
  N5: U2.AIN1, C3.+, R6.Pin_0, D3.cathode
  N6: U2.AIN0, C4.+, R7.Pin_0, D4.cathode
  N7: J1.pin1, D1.anode
  N8: J1.pin3, D2.anode
  N9: J1.pin5, D3.anode
  N10: J1.pin7, D4.anode

notes:
  Mesure de courant transfo clip
  V3 220719.1400
  Mesure de courant transfo clip v3

custom parts:
  Adafruit ADS1115 16Bit I2C ADC: For microcontrollers without an analog-to-digital converter or when you want a higher-precision ADC, the ADS1115 provides 16-bit precision at 860 samples/second over I2C. The chip can be configured as 4 single-ended input channels, or two differential channels. As a nice bonus, it even includes a programmable gain amplifier, up to x16, to help boost up smaller single/differential signals to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
  Vertical Resistor: A generic resistor (0.25W)
