# Fritzing sketch Mesure_courant_clip_v2 (saved by Fritzing 0.9.6b)
breadboards: 1

parts:
  WeMos_D1_Mini1 = WeMos D1 Mini
  U1 = LM124-324 Quad Opamp [package="DIP (Dual Inline)"]
  U2 = Adafruit ADS1115 16Bit I2C ADC [part_number=ADS1115]
  C1 = Electrolytic Capacitor [capacitance=0.1mF package="100 mil [THT, electrolytic]"]
  R3 = Vertical Resistor [tolerance=±5% resistance=10k package=THT]
  R4 = Vertical Resistor [tolerance=±5% resistance=1k package=THT]
  D1 = Upright Rectifier Diode [part_number=1N4148 package="300 mil [THT]"]
  C2 = Electrolytic Capacitor [capacitance=0.1mF package="100 mil [THT, electrolytic]"]
  C3 = Electrolytic Capacitor [capacitance=0.1mF package="100 mil [THT, electrolytic]"]
  C4 = Electrolytic Capacitor [capacitance=0.1mF package="100 mil [THT, electrolytic]"]
  R5 = Vertical Resistor [tolerance=±5% resistance=10k package=THT]
  R6 = Vertical Resistor [tolerance=±5% resistance=10k package=THT]
  R7 = Vertical Resistor [tolerance=±5% resistance=10k package=THT]
  R8 = Vertical Resistor [tolerance=±5% resistance=1k package=THT]
  R9 = Vertical Resistor [tolerance=±5% resistance=1k package=THT]
  R10 = Vertical Resistor [tolerance=±5% resistance=1k package=THT]
  D2 = Upright Rectifier Diode [part_number=1N4148 package="300 mil [THT]"]
  D3 = Upright Rectifier Diode [part_number=1N4148 package="300 mil [THT]"]
  D4 = Upright Rectifier Diode [part_number=1N4148 package="300 mil [THT]"]
  J1 = Camdenboss CTB0158-8 [part_number=CTB0158-8 package=THT]
  R11 = Resistor [tolerance=±5% resistance=220 power=0.25 package=THT]
  R12 = Resistor [tolerance=±5% resistance=220 power=0.25 package=THT]
  R13 = Resistor [tolerance=±5% resistance=220 power=0.25 package=THT]
  R14 = Resistor [tolerance=±5% resistance=220 power=0.25 package=THT]

nets (from the schematic view):
  3V3: WeMos_D1_Mini1.3V3, U2.VDD
  N1: WeMos_D1_Mini1.5V, U1.VCC+
  N2: WeMos_D1_Mini1.D1, U2.SCL
  N3: WeMos_D1_Mini1.D2, U2.SDA
  GND: WeMos_D1_Mini1.G, U1.VCC-, U2.GND, C1.-, R4.Pin_1, C2.-, C3.-, C4.-, R8.Pin_1, R9.Pin_1, R10.Pin_1, J1.pin2, J1.pin4, J1.pin6, J1.pin8, R11.Pin_1, R12.Pin_1, R13.Pin_1, R14.Pin_1
  N4: U1.1OUT, D3.anode
  N5: U1.1IN-, R5.Pin_0, D3.cathode
  N6: U1.1IN+, J1.pin3, R12.Pin_0
  N7: U1.2IN+, J1.pin1, R11.Pin_0
  N8: U1.2IN-, R3.Pin_0, D1.cathode
  N9: U1.2OUT, D1.anode
  N10: U1.3OUT, D2.anode
  N11: U1.3IN-, R6.Pin_0, D2.cathode
  N12: U1.3IN+, J1.pin5, R14.Pin_0
  N13: U1.4IN+, J1.pin7, R13.Pin_0
  N14: U1.4IN-, R7.Pin_0, D4.cathode
  N15: U1.4OUT, D4.anode
  N16: U2.AIN3, C1.+, R3.Pin_1, R4.Pin_0
  N17: U2.AIN2, C2.+, R5.Pin_1, R8.Pin_0
  N18: U2.AIN1, C3.+, R6.Pin_1, R9.Pin_0
  N19: U2.AIN0, C4.+, R7.Pin_1, R10.Pin_0

notes:
  Mesure de courant transfo clip v2
  Mesure de courant transfo clip
  220711.

custom parts:
  Adafruit ADS1115 16Bit I2C ADC: For microcontrollers without an analog-to-digital converter or when you want a higher-precision ADC, the ADS1115 provides 16-bit precision at 860 samples/second over I2C. The chip can be configured as 4 single-ended input channels, or two differential channels. As a nice bonus, it even includes a programmable gain amplifier, up to x16, to help boost up smaller single/differential signals to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
  Vertical Resistor: A generic resistor (0.25W)
  Upright Rectifier Diode: A standard rectifier diode Based on Brendan Howell's work
