# Fritzing sketch PZEM_3_phases (saved by Fritzing 0.9.6b)
breadboards: 1

parts:
  M1 = Pzem-004t
  M2 = Pzem-004t
  M3 = Pzem-004t
  WeMos_D1_Mini1 = WeMos D1 Mini

nets:
  5V: M1.5V, M2.5V, M3.5V, WeMos_D1_Mini1.5V
  N1: M1.RX, M2.RX, M3.RX, WeMos_D1_Mini1.D2
  N2: M1.TX, M2.TX, M3.TX, WeMos_D1_Mini1.D1
  GND: M1.GND, M2.GND, M3.GND, WeMos_D1_Mini1.G

notes:
  Mesure énergie maison Crissier, 1.0.0
  vers 211004.1217

custom parts:
  Pzem-004t: Pzem-004t used for measuring AC voltage, current, active power, frequency, power factor and active energy, the module is without display function, the data is read through the TTL interface.
