# Fritzing sketch ow-th-ext-sud (saved by Fritzing 0.9.6b)
breadboards: 1

parts:
  WeMos_D1_Mini1 = WeMos D1 Mini
  DS1 = DS18B20 1-Wire Temperature Sensor [part_number=DS18B20]

nets:
  3V3: WeMos_D1_Mini1.3V3, DS1.VDD
  N1: WeMos_D1_Mini1.D1, WeMos_D1_Mini1.D2, DS1.DQ
  N2: WeMos_D1_Mini1.G, DS1.GND

notes:
  1w-ds18b20_1, 1-w ds18b20 mesure de température, 1.0.1
  1w-ds18b20_1, 21 Jun 2022 13:48:07
