# Fritzing sketch thx_hut21d (saved by Fritzing 0.9.3b)
breadboards: 1

parts:
  WeMos_D1_Mini1 = WeMos D1 Mini
  HUT21D = Humidity Temperature Sensor SHT15

nets:
  3V3: WeMos_D1_Mini1.3V3, HUT21D.VCC
  N1: WeMos_D1_Mini1.D5, HUT21D.SDA
  N2: WeMos_D1_Mini1.D6, HUT21D.SCL
  GND: WeMos_D1_Mini1.G, HUT21D.GND

notes:
  Mesure de température/humidité avec HTU21DMesure de température/humidité avec HTU21D
  v1 221008.1435
  Mesure temp/humi avec HTU21D
  C'est un HTU21D au lieu du SHT15 !
