# Fritzing sketch Mini d1 PWM1 (saved by Fritzing 0.9.6b)
circuit board: 3.5cm x 6.5cm
breadboards: 1

parts:
  Mini_d1_PWM1 = WeMos D1 Mini
  Q1 = MOSFET-NCHANNEL [package=to220v]
  R1 = Resistor [tolerance=±5% power=0.25 resistance=68 package=THT]
  C1 = Electrolytic Capacitor [capacitance=100µF voltage=35V package="100 mil [THT, electrolytic]"]
  R2 = Resistor [tolerance=±5% power=0.25 resistance=68 package=THT]
  DS1 = DS18B20 1-Wire Temperature Sensor [part_number=DS18B20]
  R3 = Resistor [tolerance=±5% power=0.25 resistance=4.7k package=THT]
  DS2 = DS18B20 1-Wire Temperature Sensor [part_number=DS18B20]
  DS3 = DS18B20 1-Wire Temperature Sensor [part_number=DS18B20]
  J3 = male pin header, 2 pins [form="♂ (male)"]
  J4 = male pin header, 2 pins [form="♂ (male)"]
  J2 = male pin header, 4 pins [form="♂ (male)"]
  J1 = male pin header, 2 pins [form="♂ (male)"]
  D1 = Rectifier Diode [part_number=1N4148 package="300 mil [THT]"]
  D2 = Rectifier Diode [part_number=1N4148 package="300 mil [THT]"]

nets:
  3.3V: Mini_d1_PWM1.3V3, DS1.VDD, R3.Pin_1, DS2.VDD, DS3.VDD, J2.pin1, D1.cathode
  N1: Mini_d1_PWM1.5V, C1.+, J1.pin2
  N2: Mini_d1_PWM1.D0, D2.cathode
  N3: Mini_d1_PWM1.D1, Q1.G, J2.pin4
  N4: Mini_d1_PWM1.D2, J2.pin3
  N5: Mini_d1_PWM1.D5, DS1.DQ, R3.Pin_0, DS2.DQ, DS3.DQ
  N6: Mini_d1_PWM1.D7, J4.pin2
  GND: Mini_d1_PWM1.G, Q1.S, R2.Pin_1, DS1.GND, DS2.GND, DS3.GND, J3.pin1, J4.pin1, J2.pin2
  N7: Mini_d1_PWM1.RST, D2.anode
  N8: Q1.D, R1.Pin_1
  N9: R1.Pin_0, C1.-, R2.Pin_0, J1.pin1
  N10: J3.pin2, D1.anode

notes:
  zf221121.1924
  Mini d1 PWM1.fzz, zf221121.1924
  Mini d1 PWM1.fzz
  3.3V-GND-SDA-SCL
  dsleep
  +
  GND
  bat Li-Ion
  i2c
  1-wire
  GND-DQ-VDD
  -PWM+
  G -D- S
