# Fritzing sketch mini-d1_generic1 (saved by Fritzing 0.9.6b)
circuit board: 4.1128cm x 6.79965cm
breadboards: 1

parts:
  Mini_D1_generic_1 = WeMos D1 Mini
  R2 = Resistor [tolerance=±5% power=0.25 resistance=10k package=THT]
  R1 = Resistor [tolerance=±5% power=0.25 resistance=150k package=THT]
  R3 = Resistor [tolerance=±5% power=0.25 resistance=4.7k package=THT]
  R4 = Resistor [tolerance=±5% power=0.25 resistance=4.7k package=THT]
  J4 = male pin header, 4 pins [form="♂ (male)"]
  J1 = male pin header, 2 pins [form="♂ (male)"]
  J6 = male pin header, 3 pins [form="♂ (male)"]
  J8 = male pin header, 8 pins [form="♂ (male)"]
  J7 = male pin header, 8 pins [form="♂ (male)"]
  J2 = male pin header, 2 pins [form="♂ (male)"]
  D2 = Rectifier Diode [part_number=1N4148 package="300 mil [THT]"]
  D1 = Rectifier Diode [part_number=1N4148 package="300 mil [THT]"]
  J3 = male pin header, 4 pins [form="♂ (male)"]
  J5 = male pin header, 4 pins [form="♂ (male)"]
  J10 = male pin header, 4 pins [form="♂ (male)"]
  J9 = male pin header, 4 pins [form="♂ (male)"]
  J11 = male pin header, 4 pins [form="♂ (male)"]

nets:
  3.3V: Mini_D1_generic_1.3V3, R3.Pin_0, R4.Pin_0, J4.pin1, J6.pin1, J7.pin1, D1.cathode, J10.pin3
  N1: Mini_D1_generic_1.5V, J8.pin1
  N2: Mini_D1_generic_1.A0, R1.Pin_0, J7.pin7, J3.pin4, J9.pin3
  N3: Mini_D1_generic_1.D0, Mini_D1_generic_1.D5, R4.Pin_1, J7.pin5, J7.pin6, D2.cathode, J5.pin4, J11.pin1
  N4: Mini_D1_generic_1.D1, J4.pin4, J8.pin6, J10.pin1
  N5: Mini_D1_generic_1.D2, J4.pin3, J8.pin5, J10.pin2
  N6: Mini_D1_generic_1.D3, J8.pin4
  N7: Mini_D1_generic_1.D4, J8.pin3
  N8: Mini_D1_generic_1.D6, R3.Pin_1, J7.pin4, J5.pin3, J11.pin2
  N9: Mini_D1_generic_1.D7, J7.pin3, J2.pin2, J3.pin3, J9.pin2
  N10: Mini_D1_generic_1.D8, J7.pin2
  GND: Mini_D1_generic_1.G, R2.Pin_1, J4.pin2, J1.pin1, J6.pin2, J8.pin2, J2.pin1, J3.pin1, J5.pin2, J10.pin4, J9.pin4, J11.pin4
  N11: Mini_D1_generic_1.RST, J7.pin8, D2.anode
  N12: Mini_D1_generic_1.RX, J8.pin7
  N13: Mini_D1_generic_1.TX, J8.pin8
  N14: R2.Pin_0, R1.Pin_1, J3.pin2, J9.pin1
  N15: J1.pin2, D1.anode
  N16: J6.pin3, J5.pin1, J11.pin3

notes:
  zf221204.1457
  zf221204.1418
  I2C/ 1-WIRE
  ADC
  dsleep
  step-up 5V
  bat Li-Ion
  GND
  +
  OUT-GND-IN
  3.3V-GND-SDA-SCL
  GND-ADC-D7-3V
  I2C SCL
  I2C SDA
  I2C 3.3V
  I2C GND
  3.3V
  D7
  I2C
  SCL-SDA-GND-3.3V
