# Fritzing sketch ThHum_meter1 (saved by Fritzing 0.9.6b)
circuit board: 20.524cm x 9.52309cm
breadboards: 1

parts:
  WeMos_D1_Mini1 = WeMos D1 Mini
  R2 = Resistor [tolerance=±5% power=0.25 resistance=10k package=THT]
  R1 = Resistor [tolerance=±5% power=0.25 resistance=150k package=THT]
  R3 = Resistor [tolerance=±5% power=0.25 resistance=4.7k package=THT]
  R4 = Resistor [tolerance=±5% power=0.25 resistance=4.7k package=THT]
  J4 = male pin header, 4 pins [form="♂ (male)"]
  J1 = male pin header, 2 pins [form="♂ (male)"]
  J6 = male pin header, 3 pins [form="♂ (male)"]
  J8 = male pin header, 8 pins [form="♂ (male)"]
  J7 = male pin header, 8 pins [form="♂ (male)"]
  J2 = male pin header, 2 pins [form="♂ (male)"]
  D2 = Rectifier Diode [part_number=1N4148 package="300 mil [THT]"]
  D1 = Rectifier Diode [part_number=1N4148 package="300 mil [THT]"]
  J5 = male pin header, 5 pins [form="♂ (male)"]
  J9 = male pin header, 4 pins [form="♂ (male)"]
  J3 = male pin header, 4 pins [form="♂ (male)"]
  J10 = male pin header, 4 pins [form="♂ (male)"]

nets:
  3.3V: WeMos_D1_Mini1.3V3, R3.Pin_0, R4.Pin_0, J4.pin1, J6.pin1, J7.pin1, D1.cathode, J9.pin3
  N1: WeMos_D1_Mini1.5V, J8.pin1
  N2: WeMos_D1_Mini1.A0, R1.Pin_0, J7.pin7, J3.pin4, J10.pin3
  N3: WeMos_D1_Mini1.D0, WeMos_D1_Mini1.D5, R4.Pin_1, J7.pin5, J7.pin6, D2.cathode, J5.pin4
  N4: WeMos_D1_Mini1.D1, J4.pin4, J8.pin6, J9.pin1
  N5: WeMos_D1_Mini1.D2, J4.pin3, J8.pin5, J9.pin2
  N6: WeMos_D1_Mini1.D3, J8.pin4
  N7: WeMos_D1_Mini1.D4, J8.pin3
  N8: WeMos_D1_Mini1.D6, R3.Pin_1, J7.pin4, J5.pin3
  N9: WeMos_D1_Mini1.D7, J7.pin3, J2.pin2, J3.pin3, J10.pin2
  N10: WeMos_D1_Mini1.D8, J7.pin2
  GND: WeMos_D1_Mini1.G, R2.Pin_1, J4.pin2, J1.pin1, J6.pin2, J8.pin2, J2.pin1, J5.pin1, J5.pin2, J9.pin4, J3.pin1, J10.pin4
  N11: WeMos_D1_Mini1.RST, J7.pin8, D2.anode
  N12: WeMos_D1_Mini1.RX, J8.pin7
  N13: WeMos_D1_Mini1.TX, J8.pin8
  N14: R2.Pin_0, R1.Pin_1, J3.pin2, J10.pin1
  N15: J1.pin2, D1.anode
  N16: J6.pin3, J5.pin5

notes:
  zf221114.1750
  zf22126.1353
  i2c/1-wire
  ADC
  dsleep
  step-up 5V
  bat Li-Ion
  GND
  +
  OUT-GND-IN
  3.3V-GND-SDA-SCL
  GND-IN
  I2C SCL
  I2C SDA
  I2C 3.3V
  I2C GND
  D7
