# Fritzing sketch solar_1_wire_temp (saved by Fritzing 0.9.6b)
breadboards: 1

parts:
  WeMos_D1_Mini1 = WeMos D1 Mini
  DS1 = DS18B20 1-Wire Temperature Sensor [part_number=DS18B20]
  DS2 = DS18B20 1-Wire Temperature Sensor [part_number=DS18B20]
  DS4 = DS18B20 1-Wire Temperature Sensor [part_number=DS18B20]
  R1 = Resistor [tolerance=±5% power=0.25 resistance=1k package=THT]
  R2 = Resistor [tolerance=±5% power=0.25 resistance=100 package=THT]

nets:
  N1: WeMos_D1_Mini1.3V3, R1.Pin_0, R2.Pin_1
  N2: WeMos_D1_Mini1.D2, DS1.DQ, DS2.DQ, DS4.DQ, R1.Pin_1
  GND: WeMos_D1_Mini1.G, DS1.GND, DS2.GND, DS4.GND
  VDD: DS1.VDD, DS2.VDD, DS4.VDD, R2.Pin_0

notes:
  Mesure de températures pour installation solaire thermique, 1.0.0
